# Fritzing sketch ActuatorWithDelay_Schema (saved by Fritzing 0.9.3b)
perfboards: 1

parts:
  NRF24L01+ = NRF24L01+ Breakout Board
  J5 = female pin header, 2 pins [form="♀ (female)" part_number="5V IN"]
  U1 = RELAY [package=relay-jzc]
  D1 = Rectifier Diode [part_number=1N4148 package="300 mil [THT]"]
  R9 = Resistor [tolerance=±5% resistance=10k package=THT]
  J6 = Screw terminal - 2 pins [part_number=INTER package=THT]
  Arduino_Pro_Mini_3_3V = Arduino Pro Mini (3.3V)
  MOSFET1 = Basic FET N-Channel [part_number=IRLML2502 package="DPak [SMD]"]
  U2 = mystery part, 3 pins [chip_label=LE33A]
  C6 = Ceramic Capacitor [capacitance=100nF package="100 mil [THT, multilayer]"]
  C7 = Electrolytic Capacitor [capacitance=100µF package="100 mil [THT, electrolytic]"]
  C8 = Electrolytic Capacitor [capacitance=1µF package="100 mil [THT, electrolytic]"]

nets:
  GND: NRF24L01+.GND, J5.pin1, R9.Pin_0, Arduino_Pro_Mini_3_3V.GND, MOSFET1.source, U2.pin2, C6.0, C7.-, C8.-
  3.3V: NRF24L01+.VCC, Arduino_Pro_Mini_3_3V.VCC, U2.pin1
  CE: NRF24L01+.CE, Arduino_Pro_Mini_3_3V.D9
  CSN: NRF24L01+.CS, Arduino_Pro_Mini_3_3V.D10
  SCK: NRF24L01+.SCK, Arduino_Pro_Mini_3_3V.SCK
  MOSI: NRF24L01+.MOSI, Arduino_Pro_Mini_3_3V.MOSI
  MISO: NRF24L01+.MISO, Arduino_Pro_Mini_3_3V.MISO
  IRQ: NRF24L01+.IRQ, Arduino_Pro_Mini_3_3V.D2
  N1: J5.pin2, U2.pin3
  N2: U1.COIL2, D1.anode, MOSFET1.drain
  N3: U1.NO, J6.pin2
  N4: U1.MAIN, J6.pin1
  5V: U1.COIL1, D1.cathode
  RELAY1: R9.Pin_1, Arduino_Pro_Mini_3_3V.D3, MOSFET1.Gate
  TX: Arduino_Pro_Mini_3_3V.D8
  RX: Arduino_Pro_Mini_3_3V.D7
  N5: C6.1, C7.+, C8.+
