# Fritzing sketch CamActuatorLion_Schema (saved by Fritzing 0.9.3b)
perfboards: 1

parts:
  NRF24L01+ = NRF24L01+ Breakout Board
  C1 = Electrolytic Capacitor [capacitance=4.7µF package="100 mil [THT, electrolytic]"]
  R5 = Resistor [tolerance=±5% resistance=100k package=THT]
  J6 = Screw terminal - 2 pins [part_number="Li-on Battery" package=THT]
  U2 = mystery part, 3 pins [chip_label=LE33 part_number="REGULATOR 3.3V"]
  C2 = Ceramic Capacitor [capacitance=100nF package="100 mil [THT, multilayer]"]
  C3 = Ceramic Capacitor [capacitance=100nF package="100 mil [THT, multilayer]"]
  C4 = Electrolytic Capacitor [capacitance=2.2µF package="100 mil [THT, electrolytic]"]
  C7 = Electrolytic Capacitor [capacitance=10µF package="300 mil [THT, electrolytic]"]
  Arduino_Pro_Mini_3_3V = Arduino Pro Mini (3.3V)
  Q2 = Basic FET N-Channel [part_number=IRLML2502 package="D2Pak [SMD]"]
  C8 = Ceramic Capacitor [capacitance=100nF package="100 mil [THT, multilayer]"]
  C9 = Ceramic Capacitor [capacitance=100nF package="100 mil [THT, multilayer]"]
  C10 = Electrolytic Capacitor [capacitance=1µF package="100 mil [THT, electrolytic]"]
  C11 = Electrolytic Capacitor [capacitance=10µF package="300 mil [THT, electrolytic]"]
  U3 = mystery part, 3 pins [chip_label=MCP1825S part_number=MCP1825S-3302E/DB]
  ESP32-CAM = ESP32 - CAM
  R1 = Resistor [tolerance=±5% resistance=470k package=THT]
  R2 = Resistor [tolerance=±5% resistance=100k package=THT]
  C12 = Electrolytic Capacitor [capacitance=1µF package="100 mil [THT, electrolytic]"]

nets:
  GND: NRF24L01+.GND, C1.-, R5.Pin_1, J6.pin2, U2.pin2, C2.0, C3.1, C4.-, C7.-, Arduino_Pro_Mini_3_3V.GND, Q2.source, R2.Pin_1, C12.-
  3.3V: NRF24L01+.VCC, C1.+, U2.pin1, C2.1, C4.+, Arduino_Pro_Mini_3_3V.VCC
  CE: NRF24L01+.CE, Arduino_Pro_Mini_3_3V.D9
  CSN: NRF24L01+.CS, Arduino_Pro_Mini_3_3V.D10
  SCK: NRF24L01+.SCK, Arduino_Pro_Mini_3_3V.SCK
  MOSI: NRF24L01+.MOSI, Arduino_Pro_Mini_3_3V.MOSI
  MISO: NRF24L01+.MISO, Arduino_Pro_Mini_3_3V.MISO
  IRQ: NRF24L01+.IRQ, Arduino_Pro_Mini_3_3V.D2
  CAM_POWER: R5.Pin_0, Arduino_Pro_Mini_3_3V.D5, Q2.Gate
  3.7V: J6.pin1, U2.pin3, C3.0, C7.+, C8.0, C11.+, U3.pin1, R1.Pin_0
  ESP32_P12: Arduino_Pro_Mini_3_3V.A2, ESP32-CAM.IO12
  ESP32_P13: Arduino_Pro_Mini_3_3V.A1, ESP32-CAM.IO13
  N1: Arduino_Pro_Mini_3_3V.A0, R1.Pin_1, R2.Pin_0, C12.+
  ESP32_TX: Arduino_Pro_Mini_3_3V.D7, ESP32-CAM.VOR
  ESP32_RX: Arduino_Pro_Mini_3_3V.D6, ESP32-CAM.VOT
  N2: Q2.drain, C8.1, C9.0, C10.-, C11.-, U3.pin2, ESP32-CAM.GND
  N3: C9.1, C10.+, U3.pin3, ESP32-CAM.3V3

notes:
  MCP1700-3302E/TO is better
  CamActuator, V1.0

custom parts:
  ESP32 - CAM: The ESP32-CAM has a very competitive small-size camera module that can operate independently as a minimum system with a footprint of only 27*40.5*4.5mm and a deep sleep current of up to 6mA.
