# Fritzing sketch CatRepellent_Schema (saved by Fritzing 0.9.3b)
perfboards: 1

parts:
  NRF24L01+ = NRF24L01+ Breakout Board
  C1 = Electrolytic Capacitor [capacitance=4.7µF package="100 mil [THT, electrolytic]"]
  Q1 = Basic FET N-Channel [part_number=IRLB8721pbf package="D2Pak [SMD]"]
  J1 = Screw terminal - 2 pins [part_number="WATER PUMP" package=THT]
  R5 = Resistor [tolerance=±5% resistance=10k package=THT]
  J6 = Screw terminal - 2 pins [part_number="12V Battery" package=THT]
  J7 = male pin header, 2 pins [form="♂ (male)" part_number="Water tank sensor"]
  U1 = mystery part, 4 pins [chip_label=D36V6F5 part_number="POLOLU D36V6F5"]
  U2 = mystery part, 3 pins [chip_label=LE33 part_number="REGULATOR 3.3V"]
  C2 = Ceramic Capacitor [capacitance=100nF package="100 mil [THT, multilayer]"]
  C3 = Ceramic Capacitor [capacitance=100nF package="100 mil [THT, multilayer]"]
  C4 = Electrolytic Capacitor [capacitance=10µF package="100 mil [THT, electrolytic]"]
  C7 = Electrolytic Capacitor [capacitance=100µF package="300 mil [THT, electrolytic]"]
  Arduino_Pro_Mini_3_3V = Arduino Pro Mini (3.3V)
  Q2 = Basic FET N-Channel [part_number=IRLML2502 package="D2Pak [SMD]"]
  R6 = Resistor [tolerance=±5% resistance=1M package=THT]
  R1 = Resistor [tolerance=±5% resistance=1M package=THT]
  R2 = Resistor [tolerance=±5% resistance=47k package=THT]
  C8 = Electrolytic Capacitor [capacitance=1µF package="100 mil [THT, electrolytic]"]

nets:
  GND: NRF24L01+.GND, C1.-, Q1.source, J6.pin2, J7.pin2, U1.pin3, U2.pin2, C2.0, C3.1, C4.-, C7.-, Arduino_Pro_Mini_3_3V.GND, Q2.source, R2.Pin_1, C8.-
  3.3V: NRF24L01+.VCC, C1.+, U2.pin1, C2.1, C4.+, Arduino_Pro_Mini_3_3V.VCC
  CE: NRF24L01+.CE, Arduino_Pro_Mini_3_3V.D9
  CSN: NRF24L01+.CS, Arduino_Pro_Mini_3_3V.D10
  SCK: NRF24L01+.SCK, Arduino_Pro_Mini_3_3V.SCK
  MOSI: NRF24L01+.MOSI, Arduino_Pro_Mini_3_3V.MOSI
  MISO: NRF24L01+.MISO, Arduino_Pro_Mini_3_3V.MISO
  IRQ: NRF24L01+.IRQ, Arduino_Pro_Mini_3_3V.D2
  N1: Q1.Gate, Q2.drain, R6.Pin_0
  N2: Q1.drain, J1.pin2
  12V: J1.pin1, J6.pin1, U1.pin1, R1.Pin_0
  5V: R5.Pin_0, U1.pin2, U2.pin3, C3.0, C7.+, R6.Pin_1
  PUMP: R5.Pin_1, Arduino_Pro_Mini_3_3V.D5, Q2.Gate
  WATER_SENSOR: J7.pin1, Arduino_Pro_Mini_3_3V.A0
  voltage: Arduino_Pro_Mini_3_3V.A1, R1.Pin_1, R2.Pin_0, C8.+

notes:
  Cat Repellent, V2.0
