# Fritzing sketch DallasTemperature_Schema (saved by Fritzing 0.9.3b)
perfboards: 1

parts:
  NRF24L01+ = NRF24L01+ Breakout Board
  C1 = Electrolytic Capacitor [capacitance=4.7µF package="100 mil [THT, electrolytic]"]
  Arduino1 = Arduino Pro Mini (3.3V)
  DS1 = DS18B20 1-Wire Temperature Sensor [part_number=DS18B20]
  R1 = Resistor [tolerance=±5% resistance=4.7k package=THT]
  R2 = Photocell (LDR) [package=THT]
  R3 = Resistor [tolerance=±5% resistance=10k package=THT]

nets:
  GND: NRF24L01+.GND, C1.-, Arduino1.GND, DS1.GND, R3.Pin_0
  3.3V: NRF24L01+.VCC, C1.+, Arduino1.VCC
  CE: NRF24L01+.CE, Arduino1.D9
  CSN: NRF24L01+.CS, Arduino1.D10
  SCK: NRF24L01+.SCK, Arduino1.SCK
  MOSI: NRF24L01+.MOSI, Arduino1.MOSI
  MISO: NRF24L01+.MISO, Arduino1.MISO
  PHOTOCELL_POWER: Arduino1.A4, R2.pin_1
  PHOTOCELL: Arduino1.A3, R2.pin_0, R3.Pin_1
  TEMP_POWER: Arduino1.A1, DS1.VDD, R1.Pin_1
  TEMP: Arduino1.A0, DS1.DQ, R1.Pin_0

notes:
  Dallas Temperature, V1.0
