# Fritzing sketch Door_Schema (saved by Fritzing 0.9.3b)
breadboards: 1

parts:
  Arduino1 = Arduino Pro Mini (3.3V)
  NRF24L01+ = NRF24L01+ Breakout Board
  C1 = Electrolytic Capacitor [capacitance=4.7µF package="100 mil [THT, electrolytic]"]
  Magnetic_Switch = SPST Switch [package=switch-spdt]
  R1 = Resistor [tolerance=±5% resistance=10M package=THT]

nets:
  GND: Arduino1.GND, NRF24L01+.GND, C1.-, Magnetic_Switch.S
  3.3V: Arduino1.VCC, NRF24L01+.VCC, C1.+, R1.Pin_1
  SCK: Arduino1.SCK, NRF24L01+.SCK
  MISO: Arduino1.MISO, NRF24L01+.MISO
  MOSI: Arduino1.MOSI, NRF24L01+.MOSI
  CSN: Arduino1.D10, NRF24L01+.CS
  CE: Arduino1.D9, NRF24L01+.CE
  SWT1: Arduino1.D2, Magnetic_Switch.P
  N1: Magnetic_Switch.O, R1.Pin_0

notes:
  Door, V1.0
