# Fritzing sketch FingerPrintAlarm_Schema (saved by Fritzing 0.9.3b)
perfboards: 1

parts:
  NRF24L01+ = NRF24L01+ Breakout Board
  C1 = Electrolytic Capacitor [capacitance=4.7µF package="100 mil [THT, electrolytic]"]
  J5 = female pin header, 2 pins [form="♀ (female)" part_number="BATTERY 3.3V"]
  Arduino1 = Arduino Pro Mini (3.3V)
  ATSHA204A = IC, DIP package, 4 pins [chip_label=IC]
  R5 = Resistor [tolerance=±5% resistance=1k package=THT]
  Grow_R503 = female pin header, 6 pins [form="♀ (female)"]
  IRLML6402 = IRLML6402 [package="TO220 [THT]"]
  R6 = Resistor [tolerance=±5% resistance=100k package=THT]
  R7 = Resistor [tolerance=±5% resistance=1k package=THT]
  C2 = Electrolytic Capacitor [capacitance=0.1µF package="100 mil [THT, electrolytic]"]
  C3 = Electrolytic Capacitor [capacitance=0.22mF package="100 mil [THT, electrolytic]"]

nets:
  GND: NRF24L01+.GND, C1.-, J5.pin2, Arduino1.GND, ATSHA204A.pin3, Grow_R503.pin2, C2.-, C3.-
  3.3V: NRF24L01+.VCC, C1.+, J5.pin1, Arduino1.VCC, ATSHA204A.pin2, R5.Pin_0, Grow_R503.pin6, IRLML6402.source, R6.Pin_0, C2.+, C3.+
  CE: NRF24L01+.CE, Arduino1.D9
  CSN: NRF24L01+.CS, Arduino1.D10
  SCK: NRF24L01+.SCK, Arduino1.SCK
  MOSI: NRF24L01+.MOSI, Arduino1.MOSI
  MISO: NRF24L01+.MISO, Arduino1.MISO
  IRQ: NRF24L01+.IRQ, Arduino1.D2
  ATSHA204A: Arduino1.A3, ATSHA204A.pin1, R5.Pin_1
  FINGER_POWER: Arduino1.D6, R7.Pin_0
  FINGER_TX: Arduino1.D5, Grow_R503.pin3
  FINGER_RX: Arduino1.D4, Grow_R503.pin4
  FINGER_WAKEUP: Arduino1.D3, Grow_R503.pin5
  N1: Grow_R503.pin1, IRLML6402.drain
  N2: IRLML6402.gate, R6.Pin_1, R7.Pin_1

notes:
  Fingerprint Alarm, V1.0
  Here to avoid reset

custom parts:
  IRLML6402: A MOSFET P-Channel Transistor
