# Fritzing sketch FingerPrintLocker_Schema (saved by Fritzing 0.9.3b)
perfboards: 1

parts:
  J5 = female pin header, 2 pins [form="♀ (female)" part_number="BATTERY 3.3V"]
  Arduino1 = Arduino Pro Mini (3.3V)
  Grow_R503 = female pin header, 6 pins [form="♀ (female)"]
  IRLML6402 = IRLML6402 [package="TO220 [THT]"]
  R6 = Resistor [tolerance=±5% resistance=100k package=THT]
  R7 = Resistor [tolerance=±5% resistance=1k package=THT]
  C2 = Electrolytic Capacitor [capacitance=0.1µF package="100 mil [THT, electrolytic]"]
  C3 = Electrolytic Capacitor [capacitance=0.22mF package="100 mil [THT, electrolytic]"]
  R8 = Resistor [tolerance=±5% resistance=10k package=THT]
  Q3 = Basic FET N-Channel [part_number=IRLML2502 package="D2Pak [SMD]"]
  LOCK = female pin header, 2 pins [form="♀ (female)"]
  R9 = Resistor [tolerance=±5% resistance=1k package=THT]
  C4 = Ceramic Capacitor [capacitance=100nF package="100 mil [THT, multilayer]"]
  C5 = Electrolytic Capacitor [capacitance=0.22mF package="100 mil [THT, electrolytic]"]
  R10 = Resistor [tolerance=±5% resistance=2 package=THT]

nets:
  3.3V: J5.pin1, Arduino1.VCC, Grow_R503.pin6, IRLML6402.source, R6.Pin_0, C2.+, C3.+, C4.1, C5.+, R10.Pin_0
  GND: J5.pin2, Arduino1.GND, Grow_R503.pin2, C2.-, C3.-, R8.Pin_1, Q3.source, C4.0, C5.-
  N1: Arduino1.D8, R9.Pin_0
  FINGER_POWER: Arduino1.D6, R7.Pin_0
  FINGER_TX: Arduino1.D5, Grow_R503.pin3
  FINGER_RX: Arduino1.D4, Grow_R503.pin4
  FINGER_WAKEUP: Arduino1.D3, Grow_R503.pin5
  N2: Grow_R503.pin1, IRLML6402.drain
  N3: IRLML6402.gate, R6.Pin_1, R7.Pin_1
  N4: R8.Pin_0, Q3.Gate, R9.Pin_1
  N5: Q3.drain, LOCK.pin2
  N6: LOCK.pin1, R10.Pin_1

notes:
  Here to avoid reset
  Finger Print Locker, 1.0

custom parts:
  IRLML6402: A MOSFET P-Channel Transistor
