# Fritzing sketch HeatingSystem_Schema (saved by Fritzing 0.9.3b)
perfboards: 1

parts:
  NRF24L01+ = NRF24L01+ Breakout Board
  U1 = RELAY [package=relay-jzc]
  D1 = Rectifier Diode [part_number=1N4148 package="300 mil [THT]"]
  R9 = Resistor [tolerance=±5% resistance=10k package=THT]
  J6 = Screw terminal - 2 pins [part_number=INTER package=THT]
  Arduino_Pro_Mini_3_3V = Arduino Pro Mini (3.3V)
  MOSFET1 = Basic FET N-Channel [part_number=IRLML2502 package="DPak [SMD]"]
  C8 = Electrolytic Capacitor [capacitance=10µF package="100 mil [THT, electrolytic]"]
  LED1 = RGB LED (com. cathode, rgb) [package="5 mm [THT]"]
  R10 = Resistor [tolerance=±5% resistance=100 package=THT]
  R11 = Resistor [tolerance=±5% resistance=100 package=THT]
  R12 = Resistor [tolerance=±5% resistance=100 package=THT]
  HLK-PM1 = HLK-PM01
  J7 = Screw terminal - 2 pins [package=THT]

nets:
  GND: NRF24L01+.GND, R9.Pin_0, Arduino_Pro_Mini_3_3V.GND, MOSFET1.source, C8.-, LED1.common_cathode, HLK-PM1.-Vo
  3.3V: NRF24L01+.VCC, Arduino_Pro_Mini_3_3V.VCC, C8.+
  CE: NRF24L01+.CE, Arduino_Pro_Mini_3_3V.D9
  CSN: NRF24L01+.CS, Arduino_Pro_Mini_3_3V.D10
  SCK: NRF24L01+.SCK, Arduino_Pro_Mini_3_3V.SCK
  MOSI: NRF24L01+.MOSI, Arduino_Pro_Mini_3_3V.MOSI
  MISO: NRF24L01+.MISO, Arduino_Pro_Mini_3_3V.MISO
  IRQ: NRF24L01+.IRQ, Arduino_Pro_Mini_3_3V.D2
  N1: U1.COIL2, D1.anode, MOSFET1.drain
  N2: U1.NO, J6.pin2
  N3: U1.MAIN, J6.pin1
  5V: U1.COIL1, D1.cathode, Arduino_Pro_Mini_3_3V.RAW, HLK-PM1.+Vo
  RELAY1: R9.Pin_1, Arduino_Pro_Mini_3_3V.D3, MOSFET1.Gate
  LED_BLUE: Arduino_Pro_Mini_3_3V.A2, R10.Pin_1
  LED_GREEN: Arduino_Pro_Mini_3_3V.A1, R11.Pin_1
  LED_RED: Arduino_Pro_Mini_3_3V.A0, R12.Pin_1
  TX: Arduino_Pro_Mini_3_3V.D8
  RX: Arduino_Pro_Mini_3_3V.D7
  N4: LED1.red_anode, R12.Pin_0
  N5: LED1.green_anode, R11.Pin_0
  N6: LED1.blue_anode, R10.Pin_0
  N7: HLK-PM1.AC#0, J7.pin2
  N8: HLK-PM1.AC#1, J7.pin1
