# Fritzing sketch KeypadAlarm_Schema (saved by Fritzing 0.9.3b)
perfboards: 1

parts:
  NRF24L01+ = NRF24L01+ Breakout Board
  C1 = Electrolytic Capacitor [capacitance=4.7µF package="100 mil [THT, electrolytic]"]
  J2 = Piezo Speaker [part_number=Piezo]
  LED1 = RGB LED (com. cathode, rgb) [package="5 mm [THT]"]
  R2 = Resistor [tolerance=±5% resistance=100 package=THT]
  R3 = Resistor [tolerance=±5% resistance=100 package=THT]
  J3 = female pin header, 7 pins [form="♀ (female)" part_number=Keyboard]
  J5 = female pin header, 2 pins [form="♀ (female)" part_number="BATTERY 3.3V"]
  Arduino1 = Arduino Pro Mini (3.3V)
  S1 = Pushbutton [package="[THT]"]
  R4 = Resistor [tolerance=±5% resistance=100k package=THT]
  ATSHA204A = IC, DIP package, 4 pins [chip_label=IC]
  R5 = Resistor [tolerance=±5% resistance=1k package=THT]

nets:
  GND: NRF24L01+.GND, C1.-, J2.pin2, LED1.common_cathode, J5.pin2, Arduino1.GND, R4.Pin_0, ATSHA204A.pin3
  3.3V: NRF24L01+.VCC, C1.+, J5.pin1, Arduino1.VCC, S1.Pin_1, S1.Pin_2, ATSHA204A.pin2, R5.Pin_0
  CE: NRF24L01+.CE, Arduino1.D9
  CSN: NRF24L01+.CS, Arduino1.D10
  SCK: NRF24L01+.SCK, Arduino1.SCK
  MOSI: NRF24L01+.MOSI, Arduino1.MOSI
  MISO: NRF24L01+.MISO, Arduino1.MISO
  IRQ: NRF24L01+.IRQ, Arduino1.D2
  PIEZO: J2.pin1, Arduino1.D5
  N1: LED1.red_anode, R3.Pin_0
  N2: LED1.green_anode, R2.Pin_0
  GREEN_LED: R2.Pin_1, Arduino1.A4
  RED_LED: R3.Pin_1, Arduino1.A5
  COL3: J3.pin1, Arduino1.A2
  COL2: J3.pin2, Arduino1.A1
  COL1: J3.pin3, Arduino1.A0
  ROW4: J3.pin4, Arduino1.D3
  ROW3: J3.pin5, Arduino1.D4
  ROW2: J3.pin6, Arduino1.D7
  ROW1: J3.pin7, Arduino1.D8
  ATSHA204A: Arduino1.A3, ATSHA204A.pin1, R5.Pin_1
  BELL: Arduino1.D6, S1.Pin_3, S1.Pin_4, R4.Pin_1

notes:
  Keypad Alarm, V1.0
