# Fritzing sketch LedActuator_Schema (saved by Fritzing 0.9.3b)
breadboards: 1

parts:
  Arduino1 = Arduino Pro Mini (3.3V)
  NRF24L01+ = NRF24L01+ Breakout Board
  C1 = Electrolytic Capacitor [capacitance=4.7µF package="100 mil [THT, electrolytic]"]
  Q1 = MOSFET-NCHANNEL [part_number="MOSFET 2N7000" package=to-92]
  J1 = Screw terminal - 2 pins [package=THT]

nets:
  GND: Arduino1.GND, NRF24L01+.GND, C1.-, Q1.S
  3.3V: Arduino1.VCC, NRF24L01+.VCC, C1.+
  SCK: Arduino1.SCK, NRF24L01+.SCK
  MISO: Arduino1.MISO, NRF24L01+.MISO
  MOSI: Arduino1.MOSI, NRF24L01+.MOSI
  CSN: Arduino1.D10, NRF24L01+.CS
  CE: Arduino1.D9, NRF24L01+.CE
  LED1: Arduino1.D3, Q1.G
  IRQ: Arduino1.D2, NRF24L01+.IRQ
  N1: Q1.D, J1.pin2
  5V: J1.pin1

notes:
  LedActuator, V1.0
