# Fritzing sketch PirWithCamera_Schema (saved by Fritzing 0.9.3b)
perfboards: 1

parts:
  NRF24L01+ = NRF24L01+ Breakout Board
  C1 = Electrolytic Capacitor [capacitance=4.7µF package="100 mil [THT, electrolytic]"]
  R5 = Resistor [tolerance=±5% resistance=10k package=THT]
  J6 = Screw terminal - 2 pins [part_number=4xAA package=THT]
  U2 = mystery part, 3 pins [chip_label=MCP1702-3302E part_number="REGULATOR 3.3V"]
  C2 = Ceramic Capacitor [capacitance=100nF package="100 mil [THT, multilayer]"]
  C3 = Ceramic Capacitor [capacitance=100nF package="100 mil [THT, multilayer]"]
  C4 = Electrolytic Capacitor [capacitance=22µF package="100 mil [THT, electrolytic]"]
  C7 = Electrolytic Capacitor [capacitance=0.22mF package="300 mil [THT, electrolytic]"]
  Arduino_Pro_Mini_3_3V = Arduino Pro Mini (3.3V)
  Q2 = Basic FET N-Channel [part_number=IRLML2502 package="D2Pak [SMD]"]
  ESP32-CAM = ESP32 - CAM
  C12 = Electrolytic Capacitor [capacitance=0.22mF package="300 mil [THT, electrolytic]"]
  R6 = Resistor [tolerance=±5% resistance=1k package=THT]
  R7 = Resistor [tolerance=±5% resistance=330 package=THT]
  LED1 = LED - 5mm [color="Red (633nm)" package="5 mm [THT]"]
  U3 = mystery part, 3 pins [chip_label="MINI PIR"]

nets:
  GND: NRF24L01+.GND, C1.-, R5.Pin_1, J6.pin2, U2.pin1, C2.0, C3.1, C4.-, C7.-, Arduino_Pro_Mini_3_3V.GND, Q2.source, ESP32-CAM.GND, C12.-, LED1.cathode, U3.pin3
  3.3V: NRF24L01+.VCC, C1.+, U2.pin3, C2.1, C4.+, Arduino_Pro_Mini_3_3V.VCC, U3.pin1
  CE: NRF24L01+.CE, Arduino_Pro_Mini_3_3V.D9
  CSN: NRF24L01+.CS, Arduino_Pro_Mini_3_3V.D10
  SCK: NRF24L01+.SCK, Arduino_Pro_Mini_3_3V.SCK
  MOSI: NRF24L01+.MOSI, Arduino_Pro_Mini_3_3V.MOSI
  MISO: NRF24L01+.MISO, Arduino_Pro_Mini_3_3V.MISO
  IRQ: NRF24L01+.IRQ, Arduino_Pro_Mini_3_3V.D2
  N1: R5.Pin_0, Q2.Gate, R6.Pin_1
  6V: J6.pin1, U2.pin2, C3.0, C7.+, C12.+
  LED: Arduino_Pro_Mini_3_3V.A2, R7.Pin_0
  CAM_POWER: Arduino_Pro_Mini_3_3V.A1, R6.Pin_0
  PIR: Arduino_Pro_Mini_3_3V.D3, U3.pin2
  N2: Q2.drain, ESP32-CAM.5V
  N3: R7.Pin_1, LED1.anode

notes:
  Pir With Camera, V1.0

custom parts:
  ESP32 - CAM: The ESP32-CAM has a very competitive small-size camera module that can operate independently as a minimum system with a footprint of only 27*40.5*4.5mm and a deep sleep current of up to 6mA.
