# Fritzing sketch Siren_Schema (saved by Fritzing 0.9.3b)
breadboards: 1

parts:
  NRF24L01+ = NRF24L01+ Breakout Board
  C1 = Electrolytic Capacitor [capacitance=4.7µF package="100 mil [THT, electrolytic]"]
  Arduino1 = Arduino Pro Mini (5V)
  Q1 = Basic FET N-Channel [part_number=IRLZ44N package="D2Pak [SMD]"]
  Power_plug1 = Power plug [part_number=5V]
  J1 = Screw terminal - 2 pins [part_number=SIREN package=THT]
  J2 = Piezo Speaker [part_number=Piezo]
  R1 = Resistor [tolerance=±5% resistance=220 package=THT]
  LED1 = RGB LED (com. cathode, rgb) [package="5 mm [THT]"]
  R2 = Resistor [tolerance=±5% resistance=220 package=THT]
  R3 = Resistor [tolerance=±5% resistance=220 package=THT]
  R4 = Resistor [tolerance=±5% resistance=330 package=THT]
  R5 = Resistor [tolerance=±5% resistance=100k package=THT]
  R6 = Resistor [tolerance=±5% resistance=100k package=THT]
  J3 = female pin header, 7 pins [form="♀ (female)" part_number=Keyboard]
  J4 = female pin header, 2 pins [form="♀ (female)" part_number="Power backup IN"]
  J5 = female pin header, 2 pins [form="♀ (female)" part_number="Power backup OUT"]
  R7 = Resistor [tolerance=±5% resistance=1k package=THT]
  J6 = Screw terminal - 2 pins [part_number="12V Battery" package=THT]

nets:
  GND: NRF24L01+.GND, C1.-, Arduino1.GND, Q1.source, J2.pin2, LED1.common_cathode, R5.Pin_1, R6.Pin_0, J5.pin2, J6.pin2
  3.3V: NRF24L01+.VCC, C1.+
  CE: NRF24L01+.CE, Arduino1.D9
  CSN: NRF24L01+.CS, Arduino1.D10
  SCK: NRF24L01+.SCK, Arduino1.SCK
  MOSI: NRF24L01+.MOSI, Arduino1.MOSI
  MISO: NRF24L01+.MISO, Arduino1.MISO
  IRQ: NRF24L01+.IRQ, Arduino1.D2
  5V: Arduino1.VCC, J5.pin1
  GREEN_LED: Arduino1.A4, R2.Pin_1
  RED_LED: Arduino1.A5, R3.Pin_1
  BATTERY_STATUS: Arduino1.A6, R7.Pin_1
  BLUE_LED: Arduino1.A3, R1.Pin_1
  COL3: Arduino1.A2, J3.pin3
  COL2: Arduino1.A1, J3.pin2
  COL1: Arduino1.A0, J3.pin1
  ROW1: Arduino1.D8, J3.pin4
  ROW2: Arduino1.D7, J3.pin5
  PIEZO: Arduino1.D6, J2.pin1
  SIREN: Arduino1.D5, R4.Pin_0
  ROW3: Arduino1.D4, J3.pin6
  ROW4: Arduino1.D3, J3.pin7
  N1: Q1.Gate, R4.Pin_1, R5.Pin_0
  N2: Q1.drain, J1.pin2
  N3: Power_plug1.VCC, R6.Pin_1, J4.pin1, R7.Pin_0
  N4: Power_plug1.GND, J4.pin2
  12V: J1.pin1, J6.pin1
  N5: R1.Pin_0, LED1.blue_anode
  N6: LED1.red_anode, R3.Pin_0
  N7: LED1.green_anode, R2.Pin_0

notes:
  Siren, V1.0
