# Fritzing sketch Siren2_Schema (saved by Fritzing 0.9.3b)
perfboards: 1

parts:
  NRF24L01+ = NRF24L01+ Breakout Board
  C1 = Electrolytic Capacitor [capacitance=4.7µF package="100 mil [THT, electrolytic]"]
  Arduino_Pro_Mini_3_3V = Arduino Pro Mini (5V)
  MOSFET1 = Basic FET N-Channel [part_number=IRLML2502 package="D2Pak [SMD]"]
  Power_plug1 = Power plug [part_number=5V]
  J1 = Screw terminal - 2 pins [part_number=SIREN package=THT]
  J2 = Piezo Speaker [part_number=Piezo]
  R2 = Resistor [tolerance=±5% resistance=330 package=THT]
  R3 = Resistor [tolerance=±5% resistance=330 package=THT]
  R5 = Resistor [tolerance=±5% resistance=100k package=THT]
  R6 = Resistor [tolerance=±5% resistance=100k package=THT]
  J4 = female pin header, 2 pins [form="♀ (female)" part_number="Power backup IN"]
  J5 = female pin header, 2 pins [form="♀ (female)" part_number="Power backup OUT"]
  J6 = Screw terminal - 2 pins [part_number="12V Battery" package=THT]
  LED1 = LED - 5mm [color="Red (633nm)" package="5 mm [THT]"]
  LED2 = LED - 5mm [color="Green (560nm)" package="5 mm [THT]"]

nets:
  GND: NRF24L01+.GND, C1.-, Arduino_Pro_Mini_3_3V.GND, MOSFET1.source, Power_plug1.GND, J2.pin2, R5.Pin_1, R6.Pin_0, J4.pin2, J5.pin2, J6.pin2, LED1.cathode, LED2.cathode
  3.3V: NRF24L01+.VCC, C1.+, Arduino_Pro_Mini_3_3V.VCC
  CE: NRF24L01+.CE, Arduino_Pro_Mini_3_3V.D9
  CSN: NRF24L01+.CS, Arduino_Pro_Mini_3_3V.D10
  SCK: NRF24L01+.SCK, Arduino_Pro_Mini_3_3V.SCK
  MOSI: NRF24L01+.MOSI, Arduino_Pro_Mini_3_3V.MOSI
  MISO: NRF24L01+.MISO, Arduino_Pro_Mini_3_3V.MISO
  IRQ: NRF24L01+.IRQ, Arduino_Pro_Mini_3_3V.D2
  GREEN_LED: Arduino_Pro_Mini_3_3V.A4, R2.Pin_1
  RED_LED: Arduino_Pro_Mini_3_3V.A5, R3.Pin_1
  BATTERY_STATUS: Arduino_Pro_Mini_3_3V.A6, Power_plug1.VCC, R6.Pin_1, J4.pin1
  5V: Arduino_Pro_Mini_3_3V.RAW, J5.pin1
  PIEZO: Arduino_Pro_Mini_3_3V.D6, J2.pin1
  SIREN: Arduino_Pro_Mini_3_3V.D5, MOSFET1.Gate, R5.Pin_0
  N1: MOSFET1.drain, J1.pin2
  12V: J1.pin1, J6.pin1
  N2: R2.Pin_0, LED2.anode
  N3: R3.Pin_0, LED1.anode
