# Fritzing sketch SoilMoisture_Schema (saved by Fritzing 0.9.3b)
breadboards: 1

parts:
  Arduino1 = Arduino Pro Mini (3.3V)
  NRF24L01+ = NRF24L01+ Breakout Board
  C1 = Electrolytic Capacitor [capacitance=4.7µF package="100 mil [THT, electrolytic]"]
  Composant2 = Soil Moisture Sensor

nets:
  GND: Arduino1.GND, NRF24L01+.GND, C1.-, Composant2.GND
  3.3V: Arduino1.VCC, NRF24L01+.VCC, C1.+
  SOIL_POWER: Arduino1.A1, Composant2.VCC
  SOIL: Arduino1.A0, Composant2.SIG
  SCK: Arduino1.SCK, NRF24L01+.SCK
  MISO: Arduino1.MISO, NRF24L01+.MISO
  MOSI: Arduino1.MOSI, NRF24L01+.MOSI
  CSN: Arduino1.D10, NRF24L01+.CS
  CE: Arduino1.D9, NRF24L01+.CE

notes:
  SoilMoisture, V1.0
