# Fritzing sketch Sound_Schema (saved by Fritzing 0.9.3b)
perfboards: 1

parts:
  NRF24L01+ = NRF24L01+ Breakout Board
  R1 = Resistor [tolerance=±5% resistance=100 package=THT]
  J5 = female pin header, 2 pins [form="♀ (female)" part_number="5V IN"]
  DFPlayer_Mini1 = DFPlayer MINI [package="DIP (Dual Inline) [THT]"]
  R7 = Resistor [tolerance=±5% resistance=1k package=THT]
  R8 = Resistor [tolerance=±5% resistance=1k package=THT]
  U1 = RELAY [package=relay-jzc]
  D1 = Rectifier Diode [part_number=1N4148 package="300 mil [THT]"]
  R9 = Resistor [tolerance=±5% resistance=100k package=THT]
  J6 = Screw terminal - 2 pins [part_number="220V IN" package=THT]
  J7 = Screw terminal - 2 pins [part_number="220V OUT" package=THT]
  Arduino1 = Arduino Pro Mini (3.3V)
  J8 = female pin header, 3 pins [form="♀ (female)" part_number=AUDIO]
  IC1 = Voltage Regulator AMS1117 [package=sot223]
  C2 = Electrolytic Capacitor [capacitance=100µF package="100 mil [THT, electrolytic]"]
  C3 = Ceramic Capacitor [capacitance=100nF package="100 mil [THT, multilayer]"]
  LED2 = LED - 5mm [color="Blue (505nm)" package="5 mm [THT]"]
  MOSFET1 = Basic FET N-Channel [part_number=IRLML2502 package="DPak [SMD]"]
  C4 = Electrolytic Capacitor [capacitance=100µF package="100 mil [THT, electrolytic]"]
  C5 = Ceramic Capacitor [capacitance=100nF package="100 mil [THT, multilayer]"]

nets:
  GND: NRF24L01+.GND, J5.pin2, DFPlayer_Mini1.GND, R9.Pin_0, Arduino1.GND, J8.pin3, IC1.GND, C2.-, C3.0, LED2.cathode, MOSFET1.source, C4.-, C5.0
  3.3V: NRF24L01+.VCC, Arduino1.VCC, IC1.OUT, C2.+, C3.1
  CE: NRF24L01+.CE, Arduino1.D9
  CSN: NRF24L01+.CS, Arduino1.D10
  SCK: NRF24L01+.SCK, Arduino1.SCK
  MOSI: NRF24L01+.MOSI, Arduino1.MOSI
  MISO: NRF24L01+.MISO, Arduino1.MISO
  IRQ: NRF24L01+.IRQ, Arduino1.D2
  N1: R1.Pin_0, LED2.anode
  LED: R1.Pin_1, Arduino1.A3
  5V: J5.pin1, DFPlayer_Mini1.VCC, U1.COIL1, D1.cathode, IC1.IN, C4.+, C5.1
  N2: DFPlayer_Mini1.RX, R7.Pin_1
  N3: DFPlayer_Mini1.TX, R8.Pin_1
  DAC_R: DFPlayer_Mini1.DAC_R, J8.pin1
  DAC_L: DFPlayer_Mini1.DAC_L, J8.pin2
  RX: R7.Pin_0, Arduino1.D7
  TX: R8.Pin_0, Arduino1.D8
  N4: U1.COIL2, D1.anode, MOSFET1.drain
  N5: U1.NO, J7.pin2
  N6: U1.MAIN, J6.pin1
  RELAY1: R9.Pin_1, Arduino1.D5, MOSFET1.Gate
  N7: J6.pin2, J7.pin1

notes:
  Sound, V1.0

custom parts:
  DFPlayer MINI: MP3 module by DFRobot.com for playing Music from an SD-Card. Supports WAV and MP3 files.
