# Fritzing sketch sketch (saved by Fritzing 0.9.3b)
breadboards: 1

parts:
  Arduino_Pro_Mini_(3_3V) = Arduino Pro Mini (3.3V)
  V5 = DC Power [voltage=5V]
  R3 = Resistor [tolerance=±5% resistance=10k package=THT]
  MOSFET2 = MOSFET-NCHANNEL [part_number=2N7000 package=to-92]
  Relay_5V = RELAY [package=relay-t9a]
  Sector = AC Power [voltage=220V frequency=60]
  D2 = Rectifier Diode [part_number=1N4007 package="300 mil [THT]"]
  J1 = Screw terminal - 2 pins [package=THT]
  NRF24L01+ = NRF24L01+ Breakout Board
  U1 = MOC3031-M [part_number=MOC3041 package=dil06]
  R4 = Resistor [tolerance=±5% resistance=100 package=THT]
  R5 = Resistor [tolerance=±5% resistance=1k power=1W package=THT]
  J2 = Screw terminal - 2 pins [package=THT]
  BTA08-600BW = TRIAC [package=to-92]
  Sector_2 = AC Power [voltage=220V frequency=60]

nets:
  3.3V: Arduino_Pro_Mini_(3_3V).VCC, NRF24L01+.VCC
  GND: Arduino_Pro_Mini_(3_3V).GND, V5.V-, R3.Pin_0, MOSFET2.S, NRF24L01+.GND, U1.2
  5V: Arduino_Pro_Mini_(3_3V).RAW, V5.V+, Relay_5V.COIL1, D2.cathode
  triacX: Arduino_Pro_Mini_(3_3V).D8, Arduino_Pro_Mini_(3_3V).D7, Arduino_Pro_Mini_(3_3V).D6, R4.Pin_0
  relayX: R3.Pin_1, MOSFET2.G
  N1: MOSFET2.D, Relay_5V.COIL2, D2.anode
  N2: Relay_5V.MAIN, Sector.V+
  N3: Relay_5V.NO, J1.pin2
  N4: Sector.V-, J1.pin1
  N5: U1.1, R4.Pin_1
  N6: U1.4, R5.Pin_0
  N7: U1.6, BTA08-600BW.M2, Sector_2.V+
  N8: R5.Pin_1, BTA08-600BW.G
  N9: J2.pin1, Sector_2.V-
  N10: J2.pin2, BTA08-600BW.M1

notes:
  G
  A1
  A2
