# Fritzing sketch Motherboard_Schema (saved by Fritzing 0.9.3b)
perfboards: 1

parts:
  NRF24L01+ = NRF24L01+ Breakout Board
  IC1 = Voltage Regulator AMS1117 [package=sot223]
  C2 = Electrolytic Capacitor [capacitance=100µF package="100 mil [THT, electrolytic]"]
  C3 = Ceramic Capacitor [capacitance=100nF package="100 mil [THT, multilayer]"]
  C4 = Electrolytic Capacitor [capacitance=100µF package="100 mil [THT, electrolytic]"]
  C5 = Ceramic Capacitor [capacitance=100nF package="100 mil [THT, multilayer]"]
  Arduino_Nano = Arduino Nano (Rev3.0)
  J6 = Screw terminal - 2 pins [part_number="5V IN" package=THT]
  J7 = female pin header, 5 pins [form="♀ (female)" part_number=SWITCHES]
  DFPlayer_Mini = DFPlayer MINI [package="DIP (Dual Inline) [THT]"]
  R9 = Resistor [tolerance=±5% resistance=1k package=THT]
  R10 = Resistor [tolerance=±5% resistance=1k package=THT]
  J8 = Screw terminal - 2 pins [part_number=SPEAKER package=THT]
  U1 = RF-LINK_RX [package=rf-link_rx]
  U2 = RF-LINK_TX [package=rf-link_tx]
  C6 = Ceramic Capacitor [capacitance=100nF package="100 mil [THT, multilayer]"]
  C7 = Electrolytic Capacitor [capacitance=0.1µF package="100 mil [THT, electrolytic]"]
  C8 = Electrolytic Capacitor [capacitance=10µF package="100 mil [THT, electrolytic]"]
  J9 = Piezo Speaker [part_number="ACTIVE BUZZER"]

nets:
  GND: NRF24L01+.GND, IC1.GND, C2.-, C3.0, C4.-, C5.0, Arduino_Nano.GND, J6.pin1, J7.pin2, DFPlayer_Mini.GND, U1.GND, U2.GND, C6.0, C7.-, C8.-, J9.pin2
  3.3V: NRF24L01+.VCC, IC1.OUT, C2.+, C3.1
  CE: NRF24L01+.CE, Arduino_Nano.D9
  CSN: NRF24L01+.CS, Arduino_Nano.D10
  SCK: NRF24L01+.SCK, Arduino_Nano.D13/SCK
  MOSI: NRF24L01+.MOSI, Arduino_Nano.D11/MOSI
  MISO: NRF24L01+.MISO, Arduino_Nano.D12/MISO
  IRQ: NRF24L01+.IRQ, Arduino_Nano.D2
  5V: IC1.IN, C4.+, C5.1, Arduino_Nano.5V, J6.pin2, J7.pin1, DFPlayer_Mini.VCC, U1.+5V, U2.+5V, C6.1, C7.+, C8.+
  RF_RECEIVER: Arduino_Nano.D3, U1.DATA
  RF_TRANSMITTER: Arduino_Nano.D4, U2.DATA
  BUZZER: Arduino_Nano.D5, J9.pin1
  AUDIO_TX: Arduino_Nano.D6, R9.Pin_0
  AUDIO_RX: Arduino_Nano.D7, R10.Pin_0
  POWER_PROBE: Arduino_Nano.D8
  SWITCH_3: Arduino_Nano.A2, J7.pin5
  SWITCH_2: Arduino_Nano.A1, J7.pin4
  SWITCH_1: Arduino_Nano.A0, J7.pin3
  N1: DFPlayer_Mini.RX, R10.Pin_1
  N2: DFPlayer_Mini.TX, R9.Pin_1
  N3: DFPlayer_Mini.SPK1, J8.pin2
  N4: DFPlayer_Mini.SPK2, J8.pin1

custom parts:
  DFPlayer MINI: MP3 module by DFRobot.com for playing Music from an SD-Card. Supports WAV and MP3 files.
