# Fritzing sketch sketch (saved by Fritzing 0.9.3b)
breadboards: 1

parts:
  V5 = DC Power [voltage=5V]
  NRF24L01+ = NRF24L01+ Breakout Board
  J3 = Screw terminal - 2 pins [package=THT]
  J4 = Screw terminal - 2 pins [package=THT]
  DS3 = DS18B20 1-Wire Temperature Sensor [part_number=DS18B20]
  R6 = Resistor [tolerance=±5% resistance=4.7k package=THT]
  Arduino_Nano = Arduino Nano (Rev3.0)

nets:
  5V: V5.V+
  GND: V5.V-, NRF24L01+.GND, J3.pin2, J4.pin2, DS3.GND, Arduino_Nano.GND
  3.3V: NRF24L01+.VCC
  CE: NRF24L01+.CE, Arduino_Nano.D9
  CSN: NRF24L01+.CS, Arduino_Nano.D10
  SCK: NRF24L01+.SCK, Arduino_Nano.D13/SCK
  MOSI: NRF24L01+.MOSI, Arduino_Nano.D11/MOSI
  MISO: NRF24L01+.MISO, Arduino_Nano.D12/MISO
  IRQ: NRF24L01+.IRQ, Arduino_Nano.D2
  sensor1: J3.pin1
  sensor2: J4.pin1
  18B20: DS3.DQ, R6.Pin_1
  alim18B20: DS3.VDD, R6.Pin_0

notes:
  pump1 sensor
  pump2 sensor
