# Fritzing sketch sensor-mat01 (saved by Fritzing 0.9.3b)
circuit board: 8.46667cm x 5.64444cm
breadboards: 1

parts:
  NRF24L01 = NRF24L01
  Part1 = Arduino Pro Mini v13
  R1 = Resistor [tolerance=±5% resistance=100k package=THT]
  S1 = Pushbutton [package=THT]

nets:
  VCC: NRF24L01.VCC, Part1.VCC, S1.leg1
  N1: NRF24L01.CSN, Part1.D10_PWM/SS
  N2: NRF24L01.MOSI, Part1.D11_PWM/MOSI
  GND: NRF24L01.GND, Part1.GND, R1.Pin_1
  N3: NRF24L01.CE, Part1.D9_PWM
  N4: NRF24L01.SCK, Part1.D13/SCK
  N5: NRF24L01.MISO, Part1.D12/MISO
  N6: Part1.D2, R1.Pin_0, S1.leg0

custom parts:
  NRF24L01: NRF24L01 module

// code stored in the sketch: nrf24l01 receiver.ino

    #include <SPI.h>
    #include "nRF24L01.h"
    #include "RF24.h"
 
    RF24 radio(9,10);
 
    const uint64_t pipes[2] = { 0xF0F0F0F0E1LL, 0xF0F0F0F0D2LL };
 
    typedef enum { role_ping_out = 1, role_pong_back } role_e;
 
    const char* role_friendly_name[] = { "invalid", "Ping out", "Pong back"};
 
    role_e role = role_pong_back;
 
    void setup(void)
    {
    Serial.begin(57600);
    pinMode(4,OUTPUT);
    radio.begin();
    radio.setRetries(15,15);
    radio.openReadingPipe(1,pipes[1]);
    radio.startListening();
    radio.printDetails();
    radio.openWritingPipe(pipes[1]);
    radio.openReadingPipe(1,pipes[0]);
    radio.startListening();
    }
 
    void loop(void)
    {
 
    if ( radio.available() )
    {
    unsigned long data = 0;
    radio.read( &data, sizeof(unsigned long) );
    Serial.println(data);
    if (data==1){digitalWrite(4,HIGH);}
    else{digitalWrite(4,LOW);}
 
    delay(20);
    }
    }

// code stored in the sketch: nrf24l01 transmitter.ino

    #include <SPI.h>
    #include "nRF24L01.h"
    #include "RF24.h"
 
    RF24 radio(9,10);
 
    const uint64_t pipes[2] = { 0xF0F0F0F0E1LL, 0xF0F0F0F0D2LL };
 
    typedef enum { role_ping_out = 1, role_pong_back } role_e;
 
    const char* role_friendly_name[] = { "invalid", "Ping out", "Pong back"};
 
    role_e role = role_pong_back;
 
    void setup(void)
    {
    Serial.begin(57600);
    pinMode(4,OUTPUT);
    radio.begin();
    radio.setRetries(15,15);
    radio.openReadingPipe(1,pipes[1]);
    radio.startListening();
    radio.printDetails();
    radio.openWritingPipe(pipes[1]);
    radio.openReadingPipe(1,pipes[0]);
    radio.startListening();
    }
 
    void loop(void)
    {
 
    if ( radio.available() )
    {
    unsigned long data = 0;
    radio.read( &data, sizeof(unsigned long) );
    Serial.println(data);
    if (data==1){digitalWrite(4,HIGH);}
    else{digitalWrite(4,LOW);}
 
    delay(20);
    }
    }
